// Logisim project breadboard_computer_simulation.circ as structural Verilog: 15 circuits, main circuit main
module main (
  input  in_1,
  input  in_2,
  input  in_3,
  input  in_4,
  input  in_5,
  input  in_6,
  input  in_7,
  input  in_8,
  input  in_9,
  input  MAR,
  input  [7:0] in_11,
  input  in_12,
  input  in_13,
  input  in_14,
  input  in_15,
  input  in_16,
  input  in_17,
  input  OUTPUT_REGISTER
);

  wire a0, a1, a2, a3, a4, a5, a6, a7, b0, b1, b2, b3, b4, b5, b6, b7, bus0, bus1, bus2, bus3, bus4, bus5,
       bus6, bus7, i0, i1, i2, i3, i4, i5, i6, i7, n0, n1, n2, n3, n4, n5, n6, n7, n74161_1_pin1,
       n74161_1_pin9, n74161_1_pin10, n74161_1_pin11, n74161_1_pin12, n74161_1_pin13, n74161_1_pin14,
       n74283_1_pin7, n74283_1_pin9, not_1_out, not_2_out, not_3_out, not_4_out, not_5_out, not_6_out,
       not_7_out, not_8_out, not_9_out, not_10_out, not_12_out, o0, o1, o2, o3, o4, o5, o6, o7, q0, q1, q2,
       q3, q4, q5, q6, q7, s0, s1, s2, s3, s4, s5, s6, s7;
  wire [7:0] ic_display_rom_1_q0, ic_display_rom_1_q1, ic_display_rom_1_q2, ic_display_rom_1_q3;

  IC_74173_quad_D_type_flip_flop ic_74173_quad_d_type_flip_flop_1 (
    .Q0(i4), .Q1(i5), .Q2(i6), .Q3(i7), .E1_active_low(not_1_out), .E2_active_low(not_1_out), .CP(in_1),
    .MR(1'b0), .OE1_active_low(1'b0), .D0(bus7), .D1(bus6), .D2(bus5), .OE2_active_low(1'b0), .D3(bus4));
  LED led_1 (.in(q7));
  LED led_2 (.in(q6));
  IC_RAM ic_ram_1 (
    .Q0(q0), .Q1(q1), .Q2(q2), .Q3(q3), .Q4(q4), .Q5(q5), .Q6(q6), .Q7(q7), .A3(a3), .WE(in_6), .clk(in_1),
    .D0(bus0), .D1(bus1), .D2(bus2), .D3(bus3), .D4(bus4), .D6(bus6), .D7(bus7), .A0(a0), .A1(a1), .A2(a2));  // open: D5
  LED led_3 (.in(q5));
  LED led_4 (.in(q4));
  LED led_5 (.in(q3));
  LED led_6 (.in(q2));
  not not_1 (not_1_out, in_14);
  IC_74173_quad_D_type_flip_flop ic_74173_quad_d_type_flip_flop_2 (
    .Q0(i0), .Q1(i1), .Q2(i2), .Q3(i3), .E1_active_low(not_1_out), .E2_active_low(not_1_out), .CP(in_1),
    .MR(1'b0), .OE1_active_low(1'b0), .D0(bus3), .D1(bus2), .D2(bus1), .OE2_active_low(1'b0), .D3(bus0));
  LED led_7 (.in(i7));
  LED led_8 (.in(i6));
  not not_2 (not_2_out, in_9);
  LED led_9 (.in(q1));
  LED led_10 (.in(q0));
  LED led_11 (.in(a3));
  LED led_12 (.in(a2));
  LED led_13 (.in(a1));
  LED led_14 (.in(i5));
  LED led_15 (.in(i4));
  LED led_16 (.in(i3));
  LED led_17 (.in(a0));
  IC_74245_octal_transceiver_down ic_74245_octal_transceiver_down_1 (
    .A1(bus0), .A2(bus1), .A3(bus2), .A4(bus3), .A5(bus4), .A6(bus5), .A7(bus6), .A8(bus7),
    .OE_active_low(not_3_out), .B1(i0), .B2(i1), .B3(i2), .B4(i3), .B5(1'b0), .B6(1'b0), .B7(1'b0),
    .B8(1'b0), .DIR(1'b0));
  LED led_18 (.in(i2));
  LED led_19 (.in(i1));
  LED led_20 (.in(i0));
  not not_3 (not_3_out, in_15);
  IC_74245_octal_transceiver_down ic_74245_octal_transceiver_down_2 (
    .A1(bus0), .A2(bus1), .A3(bus2), .A4(bus3), .A5(bus4), .A6(bus5), .A7(bus6), .A8(bus7),
    .OE_active_low(not_2_out), .B1(q0), .B2(q1), .B3(q2), .B4(q3), .B5(q4), .B6(q5), .B7(q6), .B8(q7),
    .DIR(1'b0));
  IC_74173_quad_D_type_flip_flop ic_74173_quad_d_type_flip_flop_3 (
    .Q0(a0), .Q1(a1), .Q2(a2), .Q3(a3), .E1_active_low(MAR), .E2_active_low(MAR), .CP(in_1), .MR(1'b0),
    .OE1_active_low(1'b0), .D0(bus0), .D1(bus1), .D2(bus2), .OE2_active_low(1'b0), .D3(bus3));
  LED led_21 (.in(bus7));
  LED led_22 (.in(bus6));
  not not_4 (not_4_out, in_5);
  LED led_23 (.in(bus5));
  LED led_24 (.in(bus4));
  LED led_25 (.in(bus3));
  LED led_26 (.in(bus2));
  not not_5 (not_5_out, in_12);
  not not_6 (not_6_out, in_16);
  IC_74173_quad_D_type_flip_flop ic_74173_quad_d_type_flip_flop_4 (
    .Q0(o4), .Q1(o5), .Q2(o6), .Q3(o7), .E1_active_low(not_9_out), .E2_active_low(not_9_out), .CP(in_1),
    .MR(1'b0), .OE1_active_low(1'b0), .D0(bus4), .D1(bus5), .D2(bus6), .OE2_active_low(1'b0), .D3(bus7));
  LED led_27 (.in(bus1));
  LED led_28 (.in(bus0));
  IC_74245_octal_transceiver_up ic_74245_octal_transceiver_up_1 (
    .B1(bus7), .B2(bus6), .B3(bus5), .B4(bus4), .B5(bus3), .B6(bus2), .B7(bus1), .B8(bus0),
    .OE_active_low(not_4_out), .A1(in_11[7]), .A2(in_11[6]), .A3(in_11[5]), .A4(in_11[4]), .A5(in_11[3]),
    .DIR(1'b1), .A6(in_11[2]), .A7(in_11[1]), .A8(in_11[0]));
  IC_74173_quad_D_type_flip_flop ic_74173_quad_d_type_flip_flop_5 (
    .Q0(o0), .Q1(o1), .Q2(o2), .Q3(o3), .E1_active_low(not_9_out), .E2_active_low(not_9_out), .CP(in_1),
    .MR(1'b0), .OE1_active_low(1'b0), .D0(bus0), .D1(bus1), .D2(bus2), .OE2_active_low(1'b0), .D3(bus3));
  not not_7 (not_7_out, in_4);
  IC_74245_octal_transceiver_up ic_74245_octal_transceiver_up_2 (
    .B1(bus7), .B2(bus6), .B3(bus5), .B4(bus4), .B5(bus3), .B6(bus2), .B7(bus1), .B8(bus0),
    .OE_active_low(not_5_out), .A1(s7), .A2(s6), .A3(s5), .A4(s4), .A5(s3), .DIR(1'b1), .A6(s2), .A7(s1),
    .A8(s0));
  LED led_29 (.in(s7));
  LED led_30 (.in(s6));
  LED led_31 (.in(b7));
  LED led_32 (.in(b6));
  LED led_33 (.in(b5));
  IC_74245_octal_transceiver_down ic_74245_octal_transceiver_down_3 (
    .A1(bus7), .A2(bus6), .A3(bus5), .A4(bus4), .A5(bus3), .A6(bus2), .A7(bus1), .A8(bus0),
    .OE_active_low(not_6_out), .B1(b7), .B2(b6), .B3(b5), .B4(b4), .B5(b3), .B6(b2), .B7(b1), .B8(b0),
    .DIR(1'b0));
  not not_8 (not_8_out, in_7);
  LED led_34 (.in(s5));
  LED led_35 (.in(s4));
  LED led_36 (.in(s3));
  LED led_37 (.in(s2));
  LED led_38 (.in(b4));
  LED led_39 (.in(b3));
  LED led_40 (.in(b2));
  LED led_41 (.in(b1));
  not not_9 (not_9_out, OUTPUT_REGISTER);
  _74283 #(.ShowInternalStructure("true")) u_74283_1 (
    .pin1(s5), .pin2(n5), .pin3(a5), .pin4(s4), .pin5(a4), .pin6(n4), .pin7(n74283_1_pin7), .pin15(n6),
    .pin14(a6), .pin13(s6), .pin12(a7), .pin11(n7), .pin10(s7), .pin9(n74283_1_pin9));
  LED led_42 (.in(s1));
  LED led_43 (.in(s0));
  LED led_44 (.in(b0));
  IC_74173_quad_D_type_flip_flop ic_74173_quad_d_type_flip_flop_6 (
    .Q0(b4), .Q1(b5), .Q2(b6), .Q3(b7), .E1_active_low(not_10_out), .E2_active_low(not_10_out), .CP(in_1),
    .MR(1'b0), .OE1_active_low(1'b0), .D0(bus4), .D1(bus5), .D2(bus6), .OE2_active_low(1'b0), .D3(bus7));
  LED led_45 (.in(n74161_1_pin11));
  IC_74245_octal_transceiver_down ic_74245_octal_transceiver_down_4 (
    .A1(bus7), .A2(bus6), .A3(bus5), .A4(bus4), .A5(bus3), .A6(bus2), .A7(bus1), .A8(bus0),
    .OE_active_low(not_7_out), .B1(1'b0), .B2(1'b0), .B3(1'b0), .B4(1'b0), .B5(n74161_1_pin11),
    .B6(n74161_1_pin12), .B7(n74161_1_pin13), .B8(n74161_1_pin14), .DIR(1'b0));
  IC_74245_octal_transceiver_up ic_74245_octal_transceiver_up_3 (
    .B1(bus7), .B2(bus6), .B3(bus5), .B4(bus4), .B5(bus3), .B6(bus2), .B7(bus1), .B8(bus0),
    .OE_active_low(not_8_out), .A1(a7), .A2(a6), .A3(a5), .A4(a4), .A5(a3), .DIR(1'b1), .A6(a2), .A7(a1),
    .A8(a0));
  LED led_46 (.in(a7));
  LED led_47 (.in(a6));
  LED led_48 (.in(n74161_1_pin12));
  LED led_49 (.in(n74161_1_pin13));
  LED led_50 (.in(n74161_1_pin14));
  LED led_51 (.in(a5));
  LED led_52 (.in(a4));
  LED led_53 (.in(a3));
  LED led_54 (.in(a2));
  LED overflow (.in(n74283_1_pin9));
  _7486 #(.ShowInternalStructure("true")) u_7486_1 (
    .pin1(in_13), .pin2(b4), .pin3(n4), .pin4(in_13), .pin5(b5), .pin6(n5), .pin13(b7), .pin12(in_13),
    .pin11(n7), .pin10(b6), .pin9(in_13), .pin8(n6));
  IC_74173_quad_D_type_flip_flop ic_74173_quad_d_type_flip_flop_7 (
    .Q0(b0), .Q1(b1), .Q2(b2), .Q3(b3), .E1_active_low(not_10_out), .E2_active_low(not_10_out), .CP(in_1),
    .MR(1'b0), .OE1_active_low(1'b0), .D0(bus0), .D1(bus1), .D2(bus2), .OE2_active_low(1'b0), .D3(bus3));
  IC_display_ROM ic_display_rom_1 (
    .Q1(ic_display_rom_1_q1), .Q2(ic_display_rom_1_q2), .Q3(ic_display_rom_1_q3), .Q0(ic_display_rom_1_q0),
    .D0(o0), .D1(o1), .D2(o2), .D3(o3), .D4(o4), .D5(o5), .D6(o6), .D7(o7));
  _74161 #(.ShowInternalStructure("true")) u_74161_1 (
    .pin1(n74161_1_pin1), .pin2(in_1), .pin3(bus3), .pin4(bus2), .pin5(bus1), .pin6(bus0), .pin7(in_3),
    .pin14(n74161_1_pin14), .pin13(n74161_1_pin13), .pin12(n74161_1_pin12), .pin11(n74161_1_pin11),
    .pin10(n74161_1_pin10), .pin9(n74161_1_pin9));  // open: pin15
  LED led_55 (.in(a1));
  LED led_56 (.in(a0));
  _7_Segment_Display u_7_segment_display_1 (
    .g(ic_display_rom_1_q2[3]), .f(ic_display_rom_1_q2[2]), .a(ic_display_rom_1_q2[1]),
    .b(ic_display_rom_1_q2[0]), .e(ic_display_rom_1_q2[7]), .d(ic_display_rom_1_q2[6]),
    .c(ic_display_rom_1_q2[5]), .dp(ic_display_rom_1_q2[4]));
  _74283 #(.ShowInternalStructure("true")) u_74283_2 (
    .pin1(s1), .pin2(n1), .pin3(a1), .pin4(s0), .pin5(a0), .pin6(n0), .pin7(in_13), .pin15(n2), .pin14(a2),
    .pin13(s2), .pin12(a3), .pin11(n3), .pin10(s3), .pin9(n74283_1_pin7));
  not not_10 (not_10_out, in_17);
  _7_Segment_Display u_7_segment_display_2 (
    .g(ic_display_rom_1_q3[3]), .f(ic_display_rom_1_q3[2]), .a(ic_display_rom_1_q3[1]),
    .b(ic_display_rom_1_q3[0]), .e(ic_display_rom_1_q3[7]), .d(ic_display_rom_1_q3[6]),
    .c(ic_display_rom_1_q3[5]), .dp(ic_display_rom_1_q3[4]));
  not not_11 (n74161_1_pin9, in_2);
  IC_74173_quad_D_type_flip_flop ic_74173_quad_d_type_flip_flop_8 (
    .Q0(a7), .Q1(a6), .Q2(a5), .Q3(a4), .E1_active_low(not_12_out), .E2_active_low(not_12_out), .CP(in_1),
    .MR(1'b0), .OE1_active_low(1'b0), .D0(bus7), .D1(bus6), .D2(bus5), .OE2_active_low(1'b0), .D3(bus4));
  _7_Segment_Display u_7_segment_display_3 (
    .g(ic_display_rom_1_q1[3]), .f(ic_display_rom_1_q1[2]), .a(ic_display_rom_1_q1[1]),
    .b(ic_display_rom_1_q1[0]), .e(ic_display_rom_1_q1[7]), .d(ic_display_rom_1_q1[6]),
    .c(ic_display_rom_1_q1[5]), .dp(ic_display_rom_1_q1[4]));
  _7486 #(.ShowInternalStructure("true")) u_7486_2 (
    .pin1(in_13), .pin2(b0), .pin3(n0), .pin4(in_13), .pin5(b1), .pin6(n1), .pin13(b3), .pin12(in_13),
    .pin11(n3), .pin10(b2), .pin9(in_13), .pin8(n2));
  _7_Segment_Display u_7_segment_display_4 (
    .g(ic_display_rom_1_q0[3]), .f(ic_display_rom_1_q0[2]), .a(ic_display_rom_1_q0[1]),
    .b(ic_display_rom_1_q0[0]), .e(ic_display_rom_1_q0[7]), .d(ic_display_rom_1_q0[6]),
    .c(ic_display_rom_1_q0[5]), .dp(ic_display_rom_1_q0[4]));
  not not_12 (not_12_out, in_8);
  IC_74173_quad_D_type_flip_flop ic_74173_quad_d_type_flip_flop_9 (
    .Q0(a3), .Q1(a2), .Q2(a1), .Q3(a0), .E1_active_low(not_12_out), .E2_active_low(not_12_out), .CP(in_1),
    .MR(1'b0), .OE1_active_low(1'b0), .D0(bus3), .D1(bus2), .D2(bus1), .OE2_active_low(1'b0), .D3(bus0));
  // also tied to VCC on the sheet: {n74161_1_pin1, n74161_1_pin10}

  // Other names for the same wires on the sheet: clk = in_1; ctrl_ALU_out = in_12; ctrl_ALU_sub = in_13;
  //   ctrl_IR_in = in_14; ctrl_IR_out = in_15; ctrl_MAR_in = MAR; ctrl_OR_in = OUTPUT_REGISTER; ctrl_PC_en = in_3;
  //   ctrl_PC_load = in_2; ctrl_PC_out = in_4; ctrl_Ra_in = in_8; ctrl_Ra_out = in_7; ctrl_RAM_in = in_6;
  //   ctrl_RAM_out = in_9; ctrl_Rb_in = in_17; ctrl_Rb_out = in_16

  // Notes on the sheet:
  //   RAM
  //   INSTRUCTION REGISTER
  //   SYSTEM BUS
  //   REGISTER B
  //   REGISTER A
  //   PROGRAM COUNTER
  //   ALU [a0 .. a7] is register A, [b0 .. b7] is register B, [n0 .. n7] is negated content of register B,  [s0 .. s7] is result
endmodule

module system_bus (
  input  in_1,
  input  [7:0] in_2
);

  wire bus0, bus1, bus2, bus3, bus4, bus5, bus6, bus7, not_1_out;

  not not_1 (not_1_out, in_1);
  LED led_1 (.in(bus6));
  LED led_2 (.in(bus5));
  LED led_3 (.in(bus4));
  LED led_4 (.in(bus7));
  LED led_5 (.in(bus3));
  LED led_6 (.in(bus2));
  LED led_7 (.in(bus1));
  LED led_8 (.in(bus0));
  IC_74245_octal_transceiver_up ic_74245_octal_transceiver_up_1 (
    .B1(bus7), .B2(bus6), .B3(bus5), .B4(bus4), .B5(bus3), .B6(bus2), .B7(bus1), .B8(bus0),
    .OE_active_low(not_1_out), .A1(in_2[7]), .A2(in_2[6]), .A3(in_2[5]), .A4(in_2[4]), .A5(in_2[3]),
    .DIR(1'b1), .A6(in_2[2]), .A7(in_2[1]), .A8(in_2[0]));

  // Notes on the sheet:
  //   SYSTEM BUS
endmodule

module program_counter (
  input  in_1,
  input  in_2,
  input  in_3,
  input  in_4,
  input  in_5,
  input  [7:0] in_6
);

  wire bus0, bus1, bus2, bus3, bus4, bus5, bus6, bus7, n74161_1_pin1, n74161_1_pin9, n74161_1_pin10,
       n74161_1_pin11, n74161_1_pin12, n74161_1_pin13, n74161_1_pin14, not_1_out, not_2_out;

  not not_1 (not_1_out, in_5);
  LED led_1 (.in(bus6));
  LED led_2 (.in(bus5));
  LED led_3 (.in(bus4));
  LED led_4 (.in(bus7));
  not not_2 (not_2_out, in_3);
  LED led_5 (.in(bus3));
  LED led_6 (.in(bus2));
  LED led_7 (.in(bus1));
  LED led_8 (.in(bus0));
  IC_74245_octal_transceiver_up ic_74245_octal_transceiver_up_1 (
    .B1(bus7), .B2(bus6), .B3(bus5), .B4(bus4), .B5(bus3), .B6(bus2), .B7(bus1), .B8(bus0),
    .OE_active_low(not_1_out), .A1(in_6[7]), .A2(in_6[6]), .A3(in_6[5]), .A4(in_6[4]), .A5(in_6[3]),
    .DIR(1'b1), .A6(in_6[2]), .A7(in_6[1]), .A8(in_6[0]));
  IC_74245_octal_transceiver_down ic_74245_octal_transceiver_down_1 (
    .A1(bus7), .A2(bus6), .A3(bus5), .A4(bus4), .A5(bus3), .A6(bus2), .A7(bus1), .A8(bus0),
    .OE_active_low(not_2_out), .B1(1'b0), .B2(1'b0), .B3(1'b0), .B4(1'b0), .B5(n74161_1_pin11),
    .B6(n74161_1_pin12), .B7(n74161_1_pin13), .B8(n74161_1_pin14), .DIR(1'b0));
  LED led_9 (.in(n74161_1_pin11));
  LED led_10 (.in(n74161_1_pin12));
  LED led_11 (.in(n74161_1_pin13));
  LED led_12 (.in(n74161_1_pin14));
  _74161 #(.ShowInternalStructure("true")) u_74161_1 (
    .pin1(n74161_1_pin1), .pin2(in_4), .pin3(bus3), .pin4(bus2), .pin5(bus1), .pin6(bus0), .pin7(in_2),
    .pin14(n74161_1_pin14), .pin13(n74161_1_pin13), .pin12(n74161_1_pin12), .pin11(n74161_1_pin11),
    .pin10(n74161_1_pin10), .pin9(n74161_1_pin9));  // open: pin15
  not not_3 (n74161_1_pin9, in_1);
  // also tied to VCC on the sheet: {n74161_1_pin1, n74161_1_pin10}

  // Other names for the same wires on the sheet: clk = in_4; ctrl_PC_en = in_2; ctrl_PC_load = in_1;
  //   ctrl_PC_out = in_3

  // Notes on the sheet:
  //   SYSTEM BUS
  //   PROGRAM COUNTER
endmodule

module A_Register (
  input  in_1,
  input  in_2,
  input  in_3,
  input  in_4,
  input  [7:0] in_5
);

  wire a0, a1, a2, a3, a4, a5, a6, a7, bus0, bus1, bus2, bus3, bus4, bus5, bus6, bus7, not_1_out, not_2_out,
       not_3_out;

  not not_1 (not_1_out, in_4);
  LED led_1 (.in(bus6));
  LED led_2 (.in(bus5));
  LED led_3 (.in(bus4));
  LED led_4 (.in(bus7));
  not not_2 (not_2_out, in_1);
  LED led_5 (.in(bus3));
  LED led_6 (.in(bus2));
  LED led_7 (.in(bus1));
  LED led_8 (.in(bus0));
  IC_74245_octal_transceiver_up ic_74245_octal_transceiver_up_1 (
    .B1(bus7), .B2(bus6), .B3(bus5), .B4(bus4), .B5(bus3), .B6(bus2), .B7(bus1), .B8(bus0),
    .OE_active_low(not_1_out), .A1(in_5[7]), .A2(in_5[6]), .A3(in_5[5]), .A4(in_5[4]), .A5(in_5[3]),
    .DIR(1'b1), .A6(in_5[2]), .A7(in_5[1]), .A8(in_5[0]));
  IC_74245_octal_transceiver_up ic_74245_octal_transceiver_up_2 (
    .B1(bus7), .B2(bus6), .B3(bus5), .B4(bus4), .B5(bus3), .B6(bus2), .B7(bus1), .B8(bus0),
    .OE_active_low(not_2_out), .A1(a7), .A2(a6), .A3(a5), .A4(a4), .A5(a3), .DIR(1'b1), .A6(a2), .A7(a1),
    .A8(a0));
  LED led_9 (.in(a7));
  LED led_10 (.in(a6));
  LED led_11 (.in(a5));
  LED led_12 (.in(a4));
  LED led_13 (.in(a3));
  LED led_14 (.in(a2));
  LED led_15 (.in(a1));
  LED led_16 (.in(a0));
  IC_74173_quad_D_type_flip_flop ic_74173_quad_d_type_flip_flop_1 (
    .Q0(a7), .Q1(a6), .Q2(a5), .Q3(a4), .E1_active_low(not_3_out), .E2_active_low(not_3_out), .CP(in_3),
    .MR(1'b0), .OE1_active_low(1'b0), .D0(bus7), .D1(bus6), .D2(bus5), .OE2_active_low(1'b0), .D3(bus4));
  not not_3 (not_3_out, in_2);
  IC_74173_quad_D_type_flip_flop ic_74173_quad_d_type_flip_flop_2 (
    .Q0(a3), .Q1(a2), .Q2(a1), .Q3(a0), .E1_active_low(not_3_out), .E2_active_low(not_3_out), .CP(in_3),
    .MR(1'b0), .OE1_active_low(1'b0), .D0(bus3), .D1(bus2), .D2(bus1), .OE2_active_low(1'b0), .D3(bus0));

  // Other names for the same wires on the sheet: clk = in_3; ctrl_Ra_in = in_2; ctrl_Ra_out = in_1

  // Notes on the sheet:
  //   SYSTEM BUS
  //   A REGISTER
endmodule

module B_Register (
  input  in_1,
  input  in_2,
  input  in_3,
  input  in_4,
  input  [7:0] in_5
);

  wire b0, b1, b2, b3, b4, b5, b6, b7, bus0, bus1, bus2, bus3, bus4, bus5, bus6, bus7, not_1_out, not_2_out,
       not_3_out;

  not not_1 (not_1_out, in_4);
  LED led_1 (.in(bus6));
  LED led_2 (.in(bus5));
  LED led_3 (.in(bus4));
  LED led_4 (.in(bus7));
  not not_2 (not_2_out, in_1);
  LED led_5 (.in(bus3));
  LED led_6 (.in(bus2));
  LED led_7 (.in(bus1));
  LED led_8 (.in(bus0));
  IC_74245_octal_transceiver_up ic_74245_octal_transceiver_up_1 (
    .B1(bus7), .B2(bus6), .B3(bus5), .B4(bus4), .B5(bus3), .B6(bus2), .B7(bus1), .B8(bus0),
    .OE_active_low(not_1_out), .A1(in_5[7]), .A2(in_5[6]), .A3(in_5[5]), .A4(in_5[4]), .A5(in_5[3]),
    .DIR(1'b1), .A6(in_5[2]), .A7(in_5[1]), .A8(in_5[0]));
  LED led_9 (.in(b7));
  IC_74245_octal_transceiver_down ic_74245_octal_transceiver_down_1 (
    .A1(bus7), .A2(bus6), .A3(bus5), .A4(bus4), .A5(bus3), .A6(bus2), .A7(bus1), .A8(bus0),
    .OE_active_low(not_2_out), .B1(b7), .B2(b6), .B3(b5), .B4(b4), .B5(b3), .B6(b2), .B7(b1), .B8(b0),
    .DIR(1'b0));
  LED led_10 (.in(b6));
  LED led_11 (.in(b5));
  LED led_12 (.in(b4));
  LED led_13 (.in(b3));
  LED led_14 (.in(b2));
  LED led_15 (.in(b1));
  LED led_16 (.in(b0));
  IC_74173_quad_D_type_flip_flop ic_74173_quad_d_type_flip_flop_1 (
    .Q0(b4), .Q1(b5), .Q2(b6), .Q3(b7), .E1_active_low(not_3_out), .E2_active_low(not_3_out), .CP(in_3),
    .MR(1'b0), .OE1_active_low(1'b0), .D0(bus4), .D1(bus5), .D2(bus6), .OE2_active_low(1'b0), .D3(bus7));
  IC_74173_quad_D_type_flip_flop ic_74173_quad_d_type_flip_flop_2 (
    .Q0(b0), .Q1(b1), .Q2(b2), .Q3(b3), .E1_active_low(not_3_out), .E2_active_low(not_3_out), .CP(in_3),
    .MR(1'b0), .OE1_active_low(1'b0), .D0(bus0), .D1(bus1), .D2(bus2), .OE2_active_low(1'b0), .D3(bus3));
  not not_3 (not_3_out, in_2);

  // Other names for the same wires on the sheet: clk = in_3; ctrl_Rb_in = in_2; ctrl_Rb_out = in_1

  // Notes on the sheet:
  //   SYSTEM BUS
  //   B REGISTER
endmodule

module ALU (
  input  in_1,
  input  in_2,
  input  [7:0] in_3,
  input  in_4,
  input  [7:0] in_5,
  input  [7:0] in_6
);

  wire bus0, bus1, bus2, bus3, bus4, bus5, bus6, bus7, n0, n1, n2, n3, n4, n5, n6, n7, n74283_1_pin7,
       n74283_1_pin9, not_1_out, not_2_out, s0, s1, s2, s3, s4, s5, s6, s7;

  LED led_1 (.in(bus7));
  LED led_2 (.in(bus6));
  LED led_3 (.in(bus5));
  not not_1 (not_1_out, in_4);
  not not_2 (not_2_out, in_1);
  LED led_4 (.in(bus4));
  LED led_5 (.in(bus3));
  LED led_6 (.in(bus2));
  LED led_7 (.in(bus1));
  LED led_8 (.in(bus0));
  IC_74245_octal_transceiver_up ic_74245_octal_transceiver_up_1 (
    .B1(bus7), .B2(bus6), .B3(bus5), .B4(bus4), .B5(bus3), .B6(bus2), .B7(bus1), .B8(bus0),
    .OE_active_low(not_1_out), .A1(in_6[7]), .A2(in_6[6]), .A3(in_6[5]), .A4(in_6[4]), .A5(in_6[3]),
    .DIR(1'b1), .A6(in_6[2]), .A7(in_6[1]), .A8(in_6[0]));
  IC_74245_octal_transceiver_up ic_74245_octal_transceiver_up_2 (
    .B1(bus7), .B2(bus6), .B3(bus5), .B4(bus4), .B5(bus3), .B6(bus2), .B7(bus1), .B8(bus0),
    .OE_active_low(not_2_out), .A1(s7), .A2(s6), .A3(s5), .A4(s4), .A5(s3), .DIR(1'b1), .A6(s2), .A7(s1),
    .A8(s0));
  LED led_9 (.in(s7));
  LED led_10 (.in(s6));
  LED led_11 (.in(s5));
  LED led_12 (.in(s4));
  LED led_13 (.in(s3));
  LED led_14 (.in(s2));
  LED led_15 (.in(s1));
  LED led_16 (.in(s0));
  _74283 #(.ShowInternalStructure("true")) u_74283_1 (
    .pin1(s5), .pin2(n5), .pin3(in_3[5]), .pin4(s4), .pin5(in_3[4]), .pin6(n4), .pin7(n74283_1_pin7),
    .pin15(n6), .pin14(in_3[6]), .pin13(s6), .pin12(in_3[7]), .pin11(n7), .pin10(s7), .pin9(n74283_1_pin9));
  LED overflow (.in(n74283_1_pin9));
  _7486 #(.ShowInternalStructure("true")) u_7486_1 (
    .pin1(in_2), .pin2(in_5[4]), .pin3(n4), .pin4(in_2), .pin5(in_5[5]), .pin6(n5), .pin13(in_5[7]),
    .pin12(in_2), .pin11(n7), .pin10(in_5[6]), .pin9(in_2), .pin8(n6));
  _74283 #(.ShowInternalStructure("true")) u_74283_2 (
    .pin1(s1), .pin2(n1), .pin3(in_3[1]), .pin4(s0), .pin5(in_3[0]), .pin6(n0), .pin7(in_2), .pin15(n2),
    .pin14(in_3[2]), .pin13(s2), .pin12(in_3[3]), .pin11(n3), .pin10(s3), .pin9(n74283_1_pin7));
  _7486 #(.ShowInternalStructure("true")) u_7486_2 (
    .pin1(in_2), .pin2(in_5[0]), .pin3(n0), .pin4(in_2), .pin5(in_5[1]), .pin6(n1), .pin13(in_5[3]),
    .pin12(in_2), .pin11(n3), .pin10(in_5[2]), .pin9(in_2), .pin8(n2));

  // Other names for the same wires on the sheet: ctrl_ALU_out = in_1; ctrl_ALU_sub = in_2; a0 = in_3[0]; a1 = in_3[1];
  //   a2 = in_3[2]; a3 = in_3[3]; a4 = in_3[4]; a5 = in_3[5]; a6 = in_3[6]; a7 = in_3[7]; b0 = in_5[0]; b1 = in_5[1];
  //   b2 = in_5[2]; b3 = in_5[3]; b4 = in_5[4]; b5 = in_5[5]; b6 = in_5[6]; b7 = in_5[7]

  // Notes on the sheet:
  //   SYSTEM BUS
  //   ALU [a0 .. a7] is register A, [b0 .. b7] is register B, [n0 .. n7] is negated content of register B,  [s0 .. s7] is result
endmodule

module system_RAM (
  input  in_1,
  input  in_2,
  input  in_3,
  input  in_4,
  input  [7:0] in_5,
  input  in_6,
  input  in_7,
  input  in_8,
  input  in_9
);

  wire bus0, bus1, bus2, bus3, bus4, bus5, bus6, bus7, not_1_out, not_2_out, q0, q1, q2, q3, q4, q5, q6, q7;

  LED led_1 (.in(q7));
  LED led_2 (.in(q6));
  LED led_3 (.in(q5));
  IC_RAM ic_ram_1 (
    .Q0(q0), .Q1(q1), .Q2(q2), .Q3(q3), .Q4(q4), .Q5(q5), .Q6(q6), .Q7(q7), .A3(in_9), .WE(in_2), .clk(in_4),
    .D0(bus0), .D1(bus1), .D2(bus2), .D3(bus3), .D4(bus4), .D5(bus5), .D6(bus6), .D7(bus7), .A0(in_6),
    .A1(in_7), .A2(in_8));
  LED led_4 (.in(q4));
  LED led_5 (.in(q3));
  LED led_6 (.in(q2));
  LED led_7 (.in(q1));
  not not_1 (not_1_out, in_3);
  LED led_8 (.in(q0));
  IC_74245_octal_transceiver_down ic_74245_octal_transceiver_down_1 (
    .A1(bus0), .A2(bus1), .A3(bus2), .A4(bus3), .A5(bus4), .A6(bus5), .A7(bus6), .A8(bus7),
    .OE_active_low(not_1_out), .B1(q0), .B2(q1), .B3(q2), .B4(q3), .B5(q4), .B6(q5), .B7(q6), .B8(q7),
    .DIR(1'b0));
  LED led_9 (.in(bus7));
  LED led_10 (.in(bus6));
  not not_2 (not_2_out, in_1);
  LED led_11 (.in(bus5));
  LED led_12 (.in(bus4));
  LED led_13 (.in(bus3));
  LED led_14 (.in(bus2));
  LED led_15 (.in(bus1));
  LED led_16 (.in(bus0));
  IC_74245_octal_transceiver_up ic_74245_octal_transceiver_up_1 (
    .B1(bus7), .B2(bus6), .B3(bus5), .B4(bus4), .B5(bus3), .B6(bus2), .B7(bus1), .B8(bus0),
    .OE_active_low(not_2_out), .A1(in_5[7]), .A2(in_5[6]), .A3(in_5[5]), .A4(in_5[4]), .A5(in_5[3]),
    .DIR(1'b1), .A6(in_5[2]), .A7(in_5[1]), .A8(in_5[0]));

  // Other names for the same wires on the sheet: a0 = in_6; a1 = in_7; a2 = in_8; a3 = in_9; clk = in_4;
  //   ctrl_RAM_in = in_2; ctrl_RAM_out = in_3

  // Notes on the sheet:
  //   RAM
  //   SYSTEM BUS
endmodule

module MAR (
  input  MAR,
  input  in_2,
  input  in_3,
  input  [7:0] in_4
);

  wire a0, a1, a2, a3, bus0, bus1, bus2, bus3, bus4, bus5, bus6, bus7, not_1_out;

  LED led_1 (.in(bus7));
  LED led_2 (.in(bus6));
  LED led_3 (.in(bus5));
  not not_1 (not_1_out, in_3);
  LED led_4 (.in(a3));
  LED led_5 (.in(a2));
  LED led_6 (.in(a1));
  LED led_7 (.in(bus4));
  LED led_8 (.in(bus3));
  LED led_9 (.in(bus2));
  LED led_10 (.in(bus1));
  LED led_11 (.in(a0));
  LED led_12 (.in(bus0));
  IC_74245_octal_transceiver_up ic_74245_octal_transceiver_up_1 (
    .B1(bus7), .B2(bus6), .B3(bus5), .B4(bus4), .B5(bus3), .B6(bus2), .B7(bus1), .B8(bus0),
    .OE_active_low(not_1_out), .A1(in_4[7]), .A2(in_4[6]), .A3(in_4[5]), .A4(in_4[4]), .A5(in_4[3]),
    .DIR(1'b1), .A6(in_4[2]), .A7(in_4[1]), .A8(in_4[0]));
  IC_74173_quad_D_type_flip_flop ic_74173_quad_d_type_flip_flop_1 (
    .Q0(a0), .Q1(a1), .Q2(a2), .Q3(a3), .E1_active_low(MAR), .E2_active_low(MAR), .CP(in_2), .MR(1'b0),
    .OE1_active_low(1'b0), .D0(bus0), .D1(bus1), .D2(bus2), .OE2_active_low(1'b0), .D3(bus3));

  // Other names for the same wires on the sheet: clk = in_2; ctrl_MAR_in = MAR

  // Notes on the sheet:
  //   SYSTEM BUS
endmodule

module IR (
  input  in_1,
  input  in_2,
  input  in_3,
  input  in_4,
  input  [7:0] in_5
);

  wire bus0, bus1, bus2, bus3, bus4, bus5, bus6, bus7, i0, i1, i2, i3, i4, i5, i6, i7, not_1_out, not_2_out,
       not_3_out;

  LED led_1 (.in(bus7));
  LED led_2 (.in(bus6));
  LED led_3 (.in(bus5));
  not not_1 (not_1_out, in_4);
  IC_74173_quad_D_type_flip_flop ic_74173_quad_d_type_flip_flop_1 (
    .Q0(i4), .Q1(i5), .Q2(i6), .Q3(i7), .E1_active_low(not_2_out), .E2_active_low(not_2_out), .CP(in_3),
    .MR(1'b0), .OE1_active_low(1'b0), .D0(bus7), .D1(bus6), .D2(bus5), .OE2_active_low(1'b0), .D3(bus4));
  LED led_4 (.in(bus4));
  LED led_5 (.in(bus3));
  LED led_6 (.in(bus2));
  LED led_7 (.in(bus1));
  LED led_8 (.in(bus0));
  IC_74245_octal_transceiver_up ic_74245_octal_transceiver_up_1 (
    .B1(bus7), .B2(bus6), .B3(bus5), .B4(bus4), .B5(bus3), .B6(bus2), .B7(bus1), .B8(bus0),
    .OE_active_low(not_1_out), .A1(in_5[7]), .A2(in_5[6]), .A3(in_5[5]), .A4(in_5[4]), .A5(in_5[3]),
    .DIR(1'b1), .A6(in_5[2]), .A7(in_5[1]), .A8(in_5[0]));
  not not_2 (not_2_out, in_1);
  IC_74173_quad_D_type_flip_flop ic_74173_quad_d_type_flip_flop_2 (
    .Q0(i0), .Q1(i1), .Q2(i2), .Q3(i3), .E1_active_low(not_2_out), .E2_active_low(not_2_out), .CP(in_3),
    .MR(1'b0), .OE1_active_low(1'b0), .D0(bus3), .D1(bus2), .D2(bus1), .OE2_active_low(1'b0), .D3(bus0));
  LED led_9 (.in(i7));
  LED led_10 (.in(i6));
  LED led_11 (.in(i5));
  LED led_12 (.in(i4));
  LED led_13 (.in(i3));
  LED led_14 (.in(i2));
  LED led_15 (.in(i1));
  LED led_16 (.in(i0));
  IC_74245_octal_transceiver_down ic_74245_octal_transceiver_down_1 (
    .A1(bus0), .A2(bus1), .A3(bus2), .A4(bus3), .A5(bus4), .A6(bus5), .A7(bus6), .A8(bus7),
    .OE_active_low(not_3_out), .B1(i0), .B2(i1), .B3(i2), .B4(i3), .B5(1'b0), .B6(1'b0), .B7(1'b0),
    .B8(1'b0), .DIR(1'b0));
  not not_3 (not_3_out, in_2);

  // Other names for the same wires on the sheet: clk = in_3; ctrl_IR_in = in_1; ctrl_IR_out = in_2

  // Notes on the sheet:
  //   INSTRUCTION REGISTER
  //   SYSTEM BUS
endmodule

module Output_Register (
  input  OUTPUT_REGISTER,
  input  in_2,
  input  in_3,
  input  [7:0] in_4
);

  wire bus0, bus1, bus2, bus3, bus4, bus5, bus6, bus7, not_1_out, not_2_out, o0, o1, o2, o3, o4, o5, o6, o7;
  wire [3:0] ic_display_rom_1_q0, ic_display_rom_1_q0_2;
  wire [7:0] ic_display_rom_1_q1, ic_display_rom_1_q2, ic_display_rom_1_q3;

  not not_1 (not_1_out, in_3);
  LED led_1 (.in(bus6));
  LED led_2 (.in(bus5));
  LED led_3 (.in(bus4));
  LED led_4 (.in(bus7));
  IC_74173_quad_D_type_flip_flop ic_74173_quad_d_type_flip_flop_1 (
    .Q0(o4), .Q1(o5), .Q2(o6), .Q3(o7), .E1_active_low(not_2_out), .E2_active_low(not_2_out), .CP(in_2),
    .MR(1'b0), .OE1_active_low(1'b0), .D0(bus4), .D1(bus5), .D2(bus6), .OE2_active_low(1'b0), .D3(bus7));
  LED led_5 (.in(bus3));
  LED led_6 (.in(bus2));
  LED led_7 (.in(bus1));
  LED led_8 (.in(bus0));
  IC_74245_octal_transceiver_up ic_74245_octal_transceiver_up_1 (
    .B1(bus7), .B2(bus6), .B3(bus5), .B4(bus4), .B5(bus3), .B6(bus2), .B7(bus1), .B8(bus0),
    .OE_active_low(not_1_out), .A1(in_4[7]), .A2(in_4[6]), .A3(in_4[5]), .A4(in_4[4]), .A5(in_4[3]),
    .DIR(1'b1), .A6(in_4[2]), .A7(in_4[1]), .A8(in_4[0]));
  IC_74173_quad_D_type_flip_flop ic_74173_quad_d_type_flip_flop_2 (
    .Q0(o0), .Q1(o1), .Q2(o2), .Q3(o3), .E1_active_low(not_2_out), .E2_active_low(not_2_out), .CP(in_2),
    .MR(1'b0), .OE1_active_low(1'b0), .D0(bus0), .D1(bus1), .D2(bus2), .OE2_active_low(1'b0), .D3(bus3));
  _7_Segment_Display u_7_segment_display_1 ();  // open: g, f, a, b, e, d, c, dp
  not not_2 (not_2_out, OUTPUT_REGISTER);
  IC_display_ROM ic_display_rom_1 (
    .Q1(ic_display_rom_1_q1), .Q2(ic_display_rom_1_q2), .Q3(ic_display_rom_1_q3),
    .Q0({ic_display_rom_1_q0_2, ic_display_rom_1_q0}), .D0(o0), .D1(o1), .D2(o2), .D3(o3), .D4(o4), .D5(o5),
    .D6(o6), .D7(o7));
  _7_Segment_Display u_7_segment_display_2 (
    .g(ic_display_rom_1_q2[3]), .f(ic_display_rom_1_q2[2]), .a(ic_display_rom_1_q2[1]),
    .b(ic_display_rom_1_q2[0]), .e(ic_display_rom_1_q2[7]), .d(ic_display_rom_1_q2[6]),
    .c(ic_display_rom_1_q2[5]), .dp(ic_display_rom_1_q2[4]));
  _7_Segment_Display u_7_segment_display_3 (
    .g(ic_display_rom_1_q3[3]), .f(ic_display_rom_1_q3[2]), .a(ic_display_rom_1_q3[1]),
    .b(ic_display_rom_1_q3[0]), .e(ic_display_rom_1_q3[7]), .d(ic_display_rom_1_q3[6]),
    .c(ic_display_rom_1_q3[5]), .dp(ic_display_rom_1_q3[4]));
  _7_Segment_Display u_7_segment_display_4 (
    .g(ic_display_rom_1_q1[3]), .f(ic_display_rom_1_q1[2]), .a(ic_display_rom_1_q1[1]),
    .b(ic_display_rom_1_q1[0]), .e(ic_display_rom_1_q1[7]), .d(ic_display_rom_1_q1[6]),
    .c(ic_display_rom_1_q1[5]), .dp(ic_display_rom_1_q1[4]));
  _7_Segment_Display u_7_segment_display_5 (
    .g(ic_display_rom_1_q0[3]), .f(ic_display_rom_1_q0[2]), .a(ic_display_rom_1_q0[1]),
    .b(ic_display_rom_1_q0[0]), .e(ic_display_rom_1_q0_2[3]), .d(ic_display_rom_1_q0_2[2]),
    .c(ic_display_rom_1_q0_2[1]), .dp(ic_display_rom_1_q0_2[0]));

  // Other names for the same wires on the sheet: clk = in_2; ctrl_OR_in = OUTPUT_REGISTER

  // Notes on the sheet:
  //   SYSTEM BUS
  //   3210
  //   7654
  //   0 = 1110 1111 = EF
  //   1 = 0010 0001 = 21
endmodule

module IC_74173_quad_D_type_flip_flop (
  input  OE1_active_low,
  input  OE2_active_low,
  input  E1_active_low,
  input  E2_active_low,
  input  CP,
  input  MR,
  input  D0,
  input  D1,
  input  D2,
  input  D3,
  output Q0,
  output Q1,
  output Q2,
  output Q3
);

  wire and_1_out, and_2_out, and_3_out, and_4_out, and_5_out, and_6_out, and_7_out, and_8_out, buffer_1_out,
       buffer_2_out, buffer_3_out, buffer_4_out, buffer_7_out, buffer_8_out, buffer_9_out, buffer_10_out,
       CP_t, d_ff_1_q, d_ff_2_q, d_ff_3_q, d_ff_4_q, E, MR_t, not_E, OE, or_2_out, or_3_out, or_4_out,
       or_5_out;

  buf buffer_1 (buffer_1_out, OE1_active_low);
  buf buffer_2 (buffer_2_out, OE2_active_low);
  buf buffer_3 (buffer_3_out, E1_active_low);
  buf buffer_4 (buffer_4_out, E2_active_low);
  buf buffer_5 (CP_t, CP);
  buf buffer_6 (MR_t, MR);
  buf buffer_7 (buffer_7_out, D0);
  buf buffer_8 (buffer_8_out, D1);
  buf buffer_9 (buffer_9_out, D2);
  buf buffer_10 (buffer_10_out, D3);
  nor nor_1 (OE, buffer_1_out, buffer_2_out);
  or or_1 (E, buffer_3_out, buffer_4_out);
  not not_1 (not_E, E);
  and and_1 (and_1_out, d_ff_1_q, E);
  and and_2 (and_2_out, not_E, buffer_7_out);
  and and_3 (and_3_out, d_ff_2_q, E);
  and and_4 (and_4_out, not_E, buffer_8_out);
  and and_5 (and_5_out, d_ff_3_q, E);
  and and_6 (and_6_out, not_E, buffer_9_out);
  and and_7 (and_7_out, d_ff_4_q, E);
  and and_8 (and_8_out, not_E, buffer_10_out);
  D_Flip_Flop d_ff_1 (.D(or_2_out), .clk(CP_t), .Q(d_ff_1_q), .reset(MR_t));  // open: Qn, preset
  or or_2 (or_2_out, and_1_out, and_2_out);
  D_Flip_Flop d_ff_2 (.D(or_3_out), .clk(CP_t), .Q(d_ff_2_q), .reset(MR_t));  // open: Qn, preset
  or or_3 (or_3_out, and_3_out, and_4_out);
  D_Flip_Flop d_ff_3 (.D(or_4_out), .clk(CP_t), .Q(d_ff_3_q), .reset(MR_t));  // open: Qn, preset
  or or_4 (or_4_out, and_5_out, and_6_out);
  D_Flip_Flop d_ff_4 (.D(or_5_out), .clk(CP_t), .Q(d_ff_4_q), .reset(MR_t));  // open: Qn, preset
  or or_5 (or_5_out, and_7_out, and_8_out);
  assign Q0 = OE ? d_ff_1_q : 1'bz;  // Controlled_Buffer controlled_buffer_1
  assign Q1 = OE ? d_ff_2_q : 1'bz;  // Controlled_Buffer controlled_buffer_2
  assign Q2 = OE ? d_ff_3_q : 1'bz;  // Controlled_Buffer controlled_buffer_3
  assign Q3 = OE ? d_ff_4_q : 1'bz;  // Controlled_Buffer controlled_buffer_4
endmodule

module IC_74245_octal_transceiver_up (
  input  DIR,
  input  OE_active_low,
  input  A1,
  input  A2,
  input  A3,
  input  A4,
  input  A5,
  input  A6,
  input  A7,
  input  A8,
  output B1,
  output B2,
  output B3,
  output B4,
  output B5,
  output B6,
  output B7,
  output B8
);

  wire and_1_out, and_2_out;

  and and_1 (and_1_out, DIR, ~OE_active_low);  // AND_Gate
  assign B1 = and_1_out ? A1 : 1'bz;  // Controlled_Buffer controlled_buffer_1
  assign B2 = and_1_out ? A2 : 1'bz;  // Controlled_Buffer controlled_buffer_2
  assign B3 = and_1_out ? A3 : 1'bz;  // Controlled_Buffer controlled_buffer_3
  assign B4 = and_1_out ? A4 : 1'bz;  // Controlled_Buffer controlled_buffer_4
  assign B5 = and_1_out ? A5 : 1'bz;  // Controlled_Buffer controlled_buffer_5
  assign B6 = and_1_out ? A6 : 1'bz;  // Controlled_Buffer controlled_buffer_6
  assign B7 = and_1_out ? A7 : 1'bz;  // Controlled_Buffer controlled_buffer_7
  assign B8 = and_1_out ? A8 : 1'bz;  // Controlled_Buffer controlled_buffer_8
  and and_2 (and_2_out, ~DIR, ~OE_active_low);  // AND_Gate
  assign A1 = and_2_out ? B1 : 1'bz;  // Controlled_Buffer controlled_buffer_9
  assign A2 = and_2_out ? B2 : 1'bz;  // Controlled_Buffer controlled_buffer_10
  assign A3 = and_2_out ? B3 : 1'bz;  // Controlled_Buffer controlled_buffer_11
  assign A4 = and_2_out ? B4 : 1'bz;  // Controlled_Buffer controlled_buffer_12
  assign A5 = and_2_out ? B5 : 1'bz;  // Controlled_Buffer controlled_buffer_13
  assign A6 = and_2_out ? B6 : 1'bz;  // Controlled_Buffer controlled_buffer_14
  assign A7 = and_2_out ? B7 : 1'bz;  // Controlled_Buffer controlled_buffer_15
  assign A8 = and_2_out ? B8 : 1'bz;  // Controlled_Buffer controlled_buffer_16
endmodule

module IC_74245_octal_transceiver_down (
  input  DIR,
  input  OE_active_low,
  input  B1,
  input  B2,
  input  B3,
  input  B4,
  input  B5,
  input  B6,
  input  B7,
  input  B8,
  output A1,
  output A2,
  output A3,
  output A4,
  output A5,
  output A6,
  output A7,
  output A8
);

  wire and_1_out, and_2_out;

  and and_1 (and_1_out, DIR, ~OE_active_low);  // AND_Gate
  assign B1 = and_1_out ? A1 : 1'bz;  // Controlled_Buffer controlled_buffer_1
  assign B2 = and_1_out ? A2 : 1'bz;  // Controlled_Buffer controlled_buffer_2
  assign B3 = and_1_out ? A3 : 1'bz;  // Controlled_Buffer controlled_buffer_3
  assign B4 = and_1_out ? A4 : 1'bz;  // Controlled_Buffer controlled_buffer_4
  assign B5 = and_1_out ? A5 : 1'bz;  // Controlled_Buffer controlled_buffer_5
  assign B6 = and_1_out ? A6 : 1'bz;  // Controlled_Buffer controlled_buffer_6
  assign B7 = and_1_out ? A7 : 1'bz;  // Controlled_Buffer controlled_buffer_7
  assign B8 = and_1_out ? A8 : 1'bz;  // Controlled_Buffer controlled_buffer_8
  and and_2 (and_2_out, ~DIR, ~OE_active_low);  // AND_Gate
  assign A1 = and_2_out ? B1 : 1'bz;  // Controlled_Buffer controlled_buffer_9
  assign A2 = and_2_out ? B2 : 1'bz;  // Controlled_Buffer controlled_buffer_10
  assign A3 = and_2_out ? B3 : 1'bz;  // Controlled_Buffer controlled_buffer_11
  assign A4 = and_2_out ? B4 : 1'bz;  // Controlled_Buffer controlled_buffer_12
  assign A5 = and_2_out ? B5 : 1'bz;  // Controlled_Buffer controlled_buffer_13
  assign A6 = and_2_out ? B6 : 1'bz;  // Controlled_Buffer controlled_buffer_14
  assign A7 = and_2_out ? B7 : 1'bz;  // Controlled_Buffer controlled_buffer_15
  assign A8 = and_2_out ? B8 : 1'bz;  // Controlled_Buffer controlled_buffer_16
endmodule

module IC_RAM (
  input  A0,
  input  A1,
  input  A2,
  input  A3,
  input  WE,
  input  clk,
  input  D0,
  input  D1,
  input  D2,
  input  D3,
  input  D4,
  input  D5,
  input  D6,
  input  D7,
  output Q0,
  output Q1,
  output Q2,
  output Q3,
  output Q4,
  output Q5,
  output Q6,
  output Q7
);

  RAM #(.addrWidth(4), .enables("line")) ram_1 (
    .addr({A3, A2, A1, A0}), .we(WE), .oe(WE), .clk(clk), .din({D7, D6, D5, D4, D3, D2, D1, D0}),
    .dout({Q7, Q6, Q5, Q4, Q3, Q2, Q1, Q0}));
endmodule

module IC_display_ROM (
  input  D0,
  input  D1,
  input  D2,
  input  D3,
  input  D4,
  input  D5,
  input  D6,
  input  D7,
  output [7:0] Q0,
  output [7:0] Q1,
  output [7:0] Q2,
  output [7:0] Q3
);

  ROM #(.dataWidth(32)) rom_1 (.addr({D7, D6, D5, D4, D3, D2, D1, D0}), .data({Q3, Q2, Q1, Q0}));
  _7_Segment_Display u_7_segment_display_1 ();  // open: g, f, a, b, e, d, c, dp

  // Notes on the sheet:
  //   contents of rom_1 (hex, n*v repeats v):
  //   e7 21
  //   3210
  //   7654
  //   0 = 1110 1111 = E7
  //   1 = 0010 0001 = 21
endmodule
